# Fritzing sketch wiring (saved by Fritzing 0.9.6b)
breadboards: 1

parts:
  Arduino_Nano_33_IoT = Arduino Nano (Rev3.0)
  LED1 = LED - 5mm [color="Red (633nm)" current=0.030 package="5 mm [THT]"]
  LED2 = LED - 5mm [color="Blue (470nm)" current=0.030 package="5 mm [THT]"]
  LED3 = LED - 5mm [color="White (8000K)" current=0.030 package="5 mm [THT]"]
  LED4 = LED - 5mm [color="Yellow (595nm)" current=0.030 package="5 mm [THT]"]
  LED5 = LED - 5mm [color="Green (560nm)" current=0.030 package="5 mm [THT]"]
  S1 = Pushbutton [package="[THT]"]
  S2 = Pushbutton [package="[THT]"]
  S3 = Pushbutton [package="[THT]"]
  S4 = Pushbutton [package="[THT]"]
  S5 = Pushbutton [package="[THT]"]
  S6 = Pushbutton [package="[THT]"]
  S7 = Pushbutton [package="[THT]"]
  LED6 = RGB LED (com. cathode, rgb) [package="5 mm [THT]"]
  R1 = Resistor [tolerance=±5% power=0.25 resistance=220 package=THT]
  R2 = Resistor [tolerance=±5% power=0.25 resistance=220 package=THT]
  R3 = Resistor [tolerance=±5% power=0.25 resistance=220 package=THT]
  R4 = Resistor [tolerance=±5% power=0.25 resistance=220 package=THT]
  R5 = Resistor [tolerance=±5% power=0.25 resistance=220 package=THT]
  R6 = Resistor [tolerance=±5% power=0.25 resistance=220 package=THT]
  R7 = Resistor [tolerance=±5% power=0.25 resistance=220 package=THT]
  R8 = Rotary Potentiometer (Small) [maximum_resistance=100kΩ package=THT]
  J1 = Piezo Speaker
  R9 = Resistor [tolerance=±5% power=0.25 resistance=220 package=THT]
  R10 = Resistor [tolerance=±5% power=0.25 resistance=220 package=THT]

nets:
  N1: Arduino_Nano_33_IoT.GND, LED1.cathode, LED2.cathode, LED3.cathode, LED4.cathode, LED5.cathode, S1.Pin_1, S1.Pin_2, S2.Pin_1, S2.Pin_2, S3.Pin_1, S3.Pin_2, S4.Pin_1, S4.Pin_2, S5.Pin_1, S5.Pin_2, S6.Pin_1, S6.Pin_2, LED6.common_cathode, R8.leg2, J1.pin1, R10.Pin_1
  N2: Arduino_Nano_33_IoT.D2, R1.Pin_0
  N3: Arduino_Nano_33_IoT.D3, R2.Pin_0
  N4: Arduino_Nano_33_IoT.D4, R8.leg1
  N5: Arduino_Nano_33_IoT.D5, R9.Pin_0
  N6: Arduino_Nano_33_IoT.D6, R3.Pin_0
  N7: Arduino_Nano_33_IoT.D7, S5.Pin_3, S5.Pin_4
  N8: Arduino_Nano_33_IoT.D8, S6.Pin_3, S6.Pin_4
  N9: Arduino_Nano_33_IoT.D9, R4.Pin_0
  N10: Arduino_Nano_33_IoT.D10, S1.Pin_3, S1.Pin_4
  N11: Arduino_Nano_33_IoT.D11/MOSI, S2.Pin_3, S2.Pin_4
  N12: Arduino_Nano_33_IoT.D12/MISO, S3.Pin_3, S3.Pin_4
  N13: Arduino_Nano_33_IoT.A5, R7.Pin_1
  N14: Arduino_Nano_33_IoT.A3, R6.Pin_1
  N15: Arduino_Nano_33_IoT.A2, R5.Pin_1
  N16: Arduino_Nano_33_IoT.A1, S7.Pin_1, S7.Pin_2, R10.Pin_0
  N17: Arduino_Nano_33_IoT.3V3, S7.Pin_3, S7.Pin_4
  N18: Arduino_Nano_33_IoT.D13/SCK, S4.Pin_3, S4.Pin_4
  N19: LED1.anode, R1.Pin_1
  N20: LED2.anode, R2.Pin_1
  N21: LED3.anode, R9.Pin_1
  N22: LED4.anode, R3.Pin_1
  N23: LED5.anode, R4.Pin_1
  N24: LED6.red_anode, R7.Pin_0
  N25: LED6.green_anode, R6.Pin_0
  N26: LED6.blue_anode, R5.Pin_0
  N27: R8.wiper, J1.pin2
